// Logisim project Computer.circ as structural Verilog: 2 circuits, main circuit Computer
module Computer (
);

  wire address_invalid, clock_2_out, cpu_1_p1, cpu_1_p4, keyboard, keyboard_1_p4, keyboard_1_p7,
       keyboard_1_p11, memWrite, most_significant_bit, or_1_out, rams_WE, read_and_write_to_ram,
       read_and_write_to_screen, screen_load, second_most_significant_bit;
  wire [12:0] _13Bits, multiplexer_1_out;
  wire [14:0] keyboard_1_p5;
  wire [15:0] cpu_1_p2, cpu_1_p3, keyboard_1_p1, keyboard_1_p6, multiplexer_2_out, multiplexer_3_out,
       ram_1_dout, subtractor_1_out;

  and and_1 (read_and_write_to_screen, ~second_most_significant_bit, most_significant_bit);  // AND_Gate
  and and_2 (read_and_write_to_ram, ~most_significant_bit, ~second_most_significant_bit);  // AND_Gate
  or or_1 (or_1_out, _13Bits[0], _13Bits[1], _13Bits[2], _13Bits[3], _13Bits[4], _13Bits[5], _13Bits[6], _13Bits[7], _13Bits[8], _13Bits[9], _13Bits[10], _13Bits[11], _13Bits[12]);
  and and_3 (address_invalid, or_1_out, most_significant_bit, second_most_significant_bit);
  and and_4 (keyboard, ~_13Bits[0], ~_13Bits[1], ~_13Bits[2], ~_13Bits[3], ~_13Bits[4], ~_13Bits[5], ~_13Bits[6], ~_13Bits[7], ~_13Bits[8], ~_13Bits[9], ~_13Bits[10], ~_13Bits[11], ~_13Bits[12], most_significant_bit, second_most_significant_bit);  // AND_Gate
  // Probe on {most_significant_bit, second_most_significant_bit, _13Bits}
  // Probe on _13Bits
  // Probe on _13Bits
  Demultiplexer #(.enable("false"), .select(2)) demultiplexer_1 (
    .out1(screen_load), .out2(rams_WE), .in(memWrite),
    .sel({second_most_significant_bit, most_significant_bit}));  // open: out0, out3
  // CPU cpu_1: pin names not known; wires that end beside it: cpu_1_p1, cpu_1_p2, cpu_1_p3, cpu_1_p4
  Clock clock_1 (.out(cpu_1_p1));
  Multiplexer #(.enable("false"), .width(13)) multiplexer_1 (
    .in0({13{1'b0}}), .in1(_13Bits), .out(multiplexer_1_out), .sel(read_and_write_to_ram));
  // Probe on keyboard_1_p5
  ROM #(.addrWidth(15), .dataWidth(16)) rom_1 (.addr(keyboard_1_p5), .data(cpu_1_p2));
  RAM #(.addrWidth(13), .dataWidth(16)) ram_1 (
    .addr(multiplexer_1_out), .we(rams_WE), .clk(clock_2_out), .din(keyboard_1_p1), .dout(ram_1_dout));  // open: oe
  Clock clock_2 (.out(clock_2_out));
  // Probe on cpu_1_p2
  // Probe on ram_1_dout
  // Probe on keyboard_1_p1
  // Keyboard keyboard_1: pin names not known; wires that end beside it: keyboard_1_p1, memWrite, {most_significant_bit, second_most_significant_bit, _13Bits}, keyboard_1_p4, keyboard_1_p5, keyboard_1_p6, keyboard_1_p7, keyboard_1_p1, _13Bits, screen_load, keyboard_1_p11
  Button button_1 (.out(cpu_1_p4));
  Multiplexer #(.enable("false"), .width(16)) multiplexer_2 (
    .in0(ram_1_dout), .in1(subtractor_1_out), .out(multiplexer_2_out), .sel(read_and_write_to_screen));
  // Probe on subtractor_1_out
  Subtractor #(.width(16)) subtractor_1 (.a(ram_1_dout), .b(16'h5fff), .out(subtractor_1_out));  // open: bin, bout
  // Probe on read_and_write_to_screen
  // Probe on multiplexer_2_out
  or or_2 (keyboard_1_p11, cpu_1_p4, keyboard_1_p4);
  Multiplexer #(.enable("false"), .width(16)) multiplexer_3 (
    .in0(multiplexer_2_out), .in1(keyboard_1_p6), .out(multiplexer_3_out), .sel(keyboard));
  Clock clock_3 (.out(keyboard_1_p7));
  Multiplexer #(.enable("false"), .width(16)) multiplexer_4 (
    .in1({16{1'b0}}), .sel(address_invalid));  // open: in0, out
  Multiplexer #(.enable("false"), .width(16)) multiplexer_5 (
    .in0(multiplexer_3_out), .in1({16{1'b0}}), .out(cpu_1_p3), .sel(address_invalid));
  // Screen screen_1: pin names not known

  // Notes on the sheet:
  //   First, finish the Memory component.
  //   When that is complete, drag the following components out and wire them together:
  //   - CPU
  //   - ROM (32K)
  //   Then, copy the internals of the Memory component over to this file and wire that up.
  //   The CPU now has a support for a "display" instruction (opcode 1111) which works the following way:
  //   CPU:
  //   	If opcode == 1111, display = 1
  //   	else: display = 0
  //   Screen:
  //   	If display = 1, refresh image from internal memory
  //   	else: do nothing (internal memory will still update if load is 1 though)
  //   For wiring, just connect the display output from the CPU directly to the display input of the Screen
  //   if MSBs are 10, screen
  //   if MSBs are 11, keyboard
  //   if MSBs are 00, ram
  //   contents of rom_1 (hex, n*v repeats v):
  //   409f 1045 527f 607e 7e00 5dbf 2dc0 8019 104a 204b 104c 204d 104e 204f 1042 8082 808a f000 1055 1090
  //   1480 647d 1dc0 5d81 7e00 1040 1081 3443 2200 5241 401b 7e00 1080 28e 5080 10c3 2e7 6103 5481 2ce
  //   4024 7e00 5dbf 2dc0 104b 8020 304e 10c8 3651 3095 10c9 3696 104b 1282 10c2 34d5 104b 12bf 10c2 34d4
  //   4053 1056 5241 2056 8005 4053 1057 5241 2057 8005 4053 5041 2047 4053 507f 2047 4053 507f 2046 4053
  //   5041 2046 4053 1dc0 5d81 7e00 1046 108b 452 5041 10c7 1103 62c2 512 4060 516 208b 7e00 1050 1240
  //   1091 3447 1092 344a 1093 344d 1094 3450 4081 104d 1083 28e 204d 4081 104d 1083 28a 204d 4081 104f
  //   1083 28e 204f 4081 104f 1083 28a 204f 4081 7e00 108b 2440 2441 10c3 4d2 2440 2441 7e00 108d 114f
  //   50ce 2440 2a40 2441 2a41 2442 2a42 1103 512 b2a 56ff 60f5 7e00 5040 1084 3442 5241 409b 7e00 8005
  //   802a 5040 8082 5040 808a 8056 8062 1042 8082 1042 808a 8099 f000 40a0 40ae
endmodule

module Memory (
  input  [14:0] address,
  input  [15:0] in,
  input  in_3,
  input  in_4,
  output [15:0] out
);

  wire address_invalid, clock_1_out, clock_2_out, keyboard, or_1_out, read_and_write_to_ram,
       read_and_write_to_screen;
  wire [12:0] multiplexer_1_out;
  wire [15:0] keyboard_1_p1, multiplexer_2_out, multiplexer_3_out, ram_1_dout, subtractor_1_out;

  and and_1 (read_and_write_to_screen, ~address[13], address[14]);  // AND_Gate
  and and_2 (read_and_write_to_ram, ~address[14], ~address[13]);  // AND_Gate
  or or_1 (or_1_out, address[0], address[1], address[2], address[3], address[4], address[5], address[6], address[7], address[8], address[9], address[10], address[11], address[12]);
  and and_3 (address_invalid, or_1_out, address[14], address[13]);
  and and_4 (keyboard, ~address[0], ~address[1], ~address[2], ~address[3], ~address[4], ~address[5], ~address[6], ~address[7], ~address[8], ~address[9], ~address[10], ~address[11], ~address[12], address[14], address[13]);  // AND_Gate
  RAM #(.addrWidth(13), .dataWidth(16)) ram_1 (
    .addr(multiplexer_1_out), .we(read_and_write_to_ram), .clk(clock_1_out), .din(in), .dout(ram_1_dout));  // open: oe
  Multiplexer #(.enable("false"), .width(13)) multiplexer_1 (
    .in0({13{1'b0}}), .in1(address[12:0]), .out(multiplexer_1_out), .sel(read_and_write_to_ram));
  Clock clock_1 (.out(clock_1_out));
  // Keyboard keyboard_1: pin names not known; wires that end beside it: keyboard_1_p1
  // Probe on ram_1_dout
  // Probe on subtractor_1_out
  Subtractor #(.width(16)) subtractor_1 (.a(ram_1_dout), .b(16'h5fff), .out(subtractor_1_out));  // open: bin, bout
  // Probe on multiplexer_2_out
  Multiplexer #(.enable("false"), .width(16)) multiplexer_2 (
    .in0(ram_1_dout), .in1(subtractor_1_out), .out(multiplexer_2_out), .sel(read_and_write_to_screen));
  // Probe on read_and_write_to_screen
  Multiplexer #(.enable("false"), .width(16)) multiplexer_3 (
    .in0(multiplexer_2_out), .in1(keyboard_1_p1), .out(multiplexer_3_out), .sel(keyboard));
  Clock clock_2 (.out(clock_2_out));
  Multiplexer #(.enable("false"), .width(16)) multiplexer_4 (
    .in0(multiplexer_3_out), .in1({16{1'b0}}), .out(out), .sel(address_invalid));
  // Probe on address
  // Probe on address[12:0]
  // Screen screen_1: pin names not known

  // Other names for the same wires on the sheet: _13Bits[12:0] = address[12:0];
  //   second_most_significant_bit = address[13]; most_significant_bit = address[14]

  // Notes on the sheet:
  //   add logic for if first bit and second bit
  //   and any other bit, then read 0 (thats over 24576)
  //   Memory
  //   Use a 16K RAM and built in Keyboard/Screen
  //   if MSBs are 10, screen
  //   if MSBs are 11, keyboard
  //   if MSBs are 00, ram
endmodule
